// Logisim project TallerLogica-Combinatorios.circ as structural Verilog: 13 circuits, main circuit sumador_simple
module sumador_simple (
  input  A,
  input  B,
  output S,
  output Cout
);

  xor xor_1 (S, A, B);
  and and_1 (Cout, A, B);
endmodule

module sumador_completo (
  input  Cin,
  input  A,
  input  B,
  output S,
  output Cout
);

  wire Sumador_Simple_2_cout, Sumador_Simple_cout, Sumador_Simple_s;

  sumador_simple Sumador_Simple (.A(A), .B(B), .S(Sumador_Simple_s), .Cout(Sumador_Simple_cout));
  sumador_simple Sumador_Simple_2 (.A(Cin), .B(Sumador_Simple_s), .S(S), .Cout(Sumador_Simple_2_cout));
  or or_1 (Cout, Sumador_Simple_cout, Sumador_Simple_2_cout);
endmodule

module sumador_4 (
  input  Cin,
  input  [3:0] A,
  input  [3:0] B,
  output [3:0] S,
  output Cout
);

  wire sumador_completo_1_cout, sumador_completo_2_cout, sumador_completo_3_cout;

  sumador_completo sumador_completo_1 (.A(A[0]), .B(B[0]), .Cin(Cin), .S(S[0]), .Cout(sumador_completo_1_cout));
  sumador_completo sumador_completo_2 (
    .A(A[1]), .B(B[1]), .Cin(sumador_completo_1_cout), .S(S[1]), .Cout(sumador_completo_2_cout));
  sumador_completo sumador_completo_3 (
    .A(A[2]), .B(B[2]), .Cin(sumador_completo_2_cout), .S(S[2]), .Cout(sumador_completo_3_cout));
  sumador_completo sumador_completo_4 (.A(A[3]), .B(B[3]), .Cin(sumador_completo_3_cout), .S(S[3]), .Cout(Cout));
  Hex_Digit_Display hex_digit_display_1 (.value(S));  // open: dp
endmodule

module comparador_cero (
  input  [3:0] A,
  output Z
);

  wire or_1_out, or_2_out, or_3_out;

  or or_1 (or_1_out, A[0], A[1]);
  or or_2 (or_2_out, or_1_out, or_3_out);
  or or_3 (or_3_out, A[2], A[3]);
  not not_1 (Z, or_2_out);
endmodule

module sumador_flags (
  input  Cin,
  input  [3:0] A,
  input  [3:0] B,
  output [3:0] S,
  output V,
  output N,
  output Z,
  output C
);

  sumador_4 Sumador_4_bits (.A(A), .B(B), .Cin(Cin), .Cout(C), .S({N, S[2:0]}));
  comparador_cero Comparador_cero (.A({N, S[2:0]}), .Z(Z));
  Hex_Digit_Display hex_digit_display_1 (.value({N, S[2:0]}));  // open: dp
  detector_overflow Detector_Overflow (.A(A), .B(B), .MSB(N), .Overflow(V));

  assign S[3] = N;
endmodule

module incrementador_4 (
  input  [3:0] A,
  output [3:0] S
);

  sumador_4 Sumador_de_4_bits (.A(A), .B(4'b0001), .Cin(1'b0), .S(S));  // open: Cout
  Hex_Digit_Display hex_digit_display_1 (.value(S));  // open: dp
endmodule

module inversor_4 (
  input  [3:0] A,
  input  INV,
  output [3:0] S
);

  wire [3:0] Incrementador_s, not_1_out;

  assign not_1_out = ~A;  // NOT_Gate not_1, 4 bits wide
  incrementador_4 Incrementador (.A(not_1_out), .S(Incrementador_s));
  Multiplexer #(.width(4), .enable("false")) multiplexer_1 (.in0(A), .in1(Incrementador_s), .out(S), .sel(INV));
  Hex_Digit_Display hex_digit_display_1 (.value(S));  // open: dp
endmodule

module ALU (
  input  [3:0] A,
  input  [3:0] B,
  input  [1:0] OP,
  output N,
  output Z,
  output V,
  output C,
  output [3:0] S
);

  wire not_1_out, Resta_c, Resta_v, Sumador_Flags_c, Sumador_Flags_v;
  wire [3:0] AND_s, Inversor_s, OR_s, Resta_s, Sumador_Flags_s;

  sumador_flags Sumador_Flags (
    .A(A), .B(B), .Cin(1'b0), .S(Sumador_Flags_s), .V(Sumador_Flags_v), .C(Sumador_Flags_c));  // open: N, Z
  inversor_4 Inversor (.A(B), .INV(1'b1), .S(Inversor_s));
  OR_4_bits OR (.A(A), .B(B), .S(OR_s));
  sumador_flags Resta (.A(A), .B(Inversor_s), .Cin(1'b0), .S(Resta_s), .V(Resta_v), .C(Resta_c));  // open: N, Z
  AND_4_bits AND (.A(A), .B(B), .S(AND_s));
  not not_1 (not_1_out, Resta_c);
  Multiplexer #(.select(2), .enable("false")) multiplexer_1 (
    .in0(Sumador_Flags_v), .in1(Resta_v), .in2(1'b0), .in3(1'b0), .out(V), .sel(OP));
  Multiplexer #(.select(2), .width(4), .enable("false")) multiplexer_2 (
    .in0(Sumador_Flags_s), .in1(Resta_s), .in2(OR_s), .in3(AND_s), .out({N, S[2:0]}), .sel(OP));
  comparador_cero comparador_cero_1 (.A({N, S[2:0]}), .Z(Z));
  Multiplexer #(.select(2), .enable("false")) multiplexer_3 (
    .in0(Sumador_Flags_c), .in1(not_1_out), .in2(1'b0), .in3(1'b0), .out(C), .sel(OP));
  Hex_Digit_Display hex_digit_display_1 (.value({N, S[2:0]}));  // open: dp

  assign S[3] = N;
endmodule

module verificador (
  output [3:0] out_1,
  output [3:0] out_2,
  output [1:0] out_3,
  output halt,
  output N,
  output Z,
  output V,
  output C,
  output [3:0] res
);

  wire clock_1_out;

  Clock clock_1 (.out(clock_1_out));
  Counter #(.width(10), .max('h3ff)) counter_1 ();  // open: load, D, count, Q, carry, clk, clr
  ALU alu_1 (.A(out_1), .B(out_2), .OP(out_3), .N(N), .Z(Z), .V(V), .C(C), .S(res));
endmodule

module detector_overflow (
  input  MSB,
  input  [3:0] A,
  input  [3:0] B,
  output Overflow
);

  wire and_1_out, and_2_out, not_1_out, not_2_out, not_3_out;

  not not_1 (not_1_out, MSB);
  not not_2 (not_2_out, A[3]);
  not not_3 (not_3_out, B[3]);
  and and_1 (and_1_out, MSB, not_2_out, not_3_out);
  and and_2 (and_2_out, not_1_out, A[3], B[3]);
  or or_1 (Overflow, and_1_out, and_2_out);
endmodule

module and_triple (
  input  A,
  input  B,
  input  C,
  output Salida
);

  wire and_1_out;

  and and_1 (and_1_out, A, B);
  and and_2 (Salida, and_1_out, C);
endmodule

module OR_4_bits (
  input  [3:0] A,
  input  [3:0] B,
  output [3:0] S
);

  or or_1 (S[0], A[0], B[0]);
  or or_2 (S[1], A[1], B[1]);
  or or_3 (S[2], A[2], B[2]);
  or or_4 (S[3], A[3], B[3]);
endmodule

module AND_4_bits (
  input  [3:0] A,
  input  [3:0] B,
  output [3:0] S
);

  and and_1 (S[0], A[0], B[0]);
  and and_2 (S[1], A[1], B[1]);
  and and_3 (S[2], A[2], B[2]);
  and and_4 (S[3], A[3], B[3]);
endmodule
